// Logisim project ALU.circ as structural Verilog: 1 circuit, main circuit ALU
module ALU (
  input  [31:0] SrcA,
  input  [31:0] SrcB,
  input  [2:0] in_3,
  output out_4,
  output [31:0] out_5
);

  wire [31:0] adder_1_out, and_1_out, bit_extender_1_out, multiplexer_1_out, not_1_out, or_1_out;

  assign not_1_out = ~SrcB;  // NOT_Gate not_1, 32 bits wide
  Multiplexer #(.width(32)) multiplexer_1 (
    .in0(SrcB), .in1(not_1_out), .out(multiplexer_1_out), .sel(in_3[2]));  // open: en
  assign and_1_out = SrcA & multiplexer_1_out;  // AND_Gate and_1, 32 bits wide
  assign or_1_out = SrcA | multiplexer_1_out;  // OR_Gate or_1, 32 bits wide
  Adder #(.width(32)) adder_1 (.a(SrcA), .b(multiplexer_1_out), .out(adder_1_out), .cin(in_3[2]));  // open: cout
  assign bit_extender_1_out = {{31{1'b0}}, adder_1_out[31]};  // Bit_Extender bit_extender_1
  Multiplexer #(.select(2), .width(32)) multiplexer_2 (
    .in0(and_1_out), .in1(or_1_out), .in2(adder_1_out), .in3(bit_extender_1_out), .out(out_5), .sel(in_3[1:0]));  // open: en
  Comparator #(.width(32)) comparator_1 (.a({32{1'b0}}), .b(out_5), .eq(out_4));  // open: gt, lt
endmodule
