// Logisim project BTB.circ as structural Verilog: 1 circuit, main circuit main
module main (
  input  [31:0] Current_PC,
  input  [31:0] TargetedAddr,
  input  Branched,
  input  CLK,
  input  Taken,
  output [31:0] TargetAddr,
  output Hit
);

  wire comparator_1_eq;
  wire [30:0] ram_1_data;
  wire [31:0] bit_extender_1_out;

  RAM #(.addrWidth(24), .dataWidth(32), .bus("separate")) ram_1 (
    .addr(Current_PC[25:2]), .din({Branched, TargetedAddr[30:0]}), .data({Hit, ram_1_data}), .str(Branched),
    .clk(CLK), .ld(Taken));  // open: sel, clr
  Comparator #(.width(5)) comparator_1 (
    .a(Current_PC[30:26]), .b(ram_1_data[30:26]), .eq(comparator_1_eq));  // open: gt, lt
  assign bit_extender_1_out = {{31{comparator_1_eq}}, comparator_1_eq};  // Bit_Extender bit_extender_1
  assign TargetAddr = bit_extender_1_out & {Hit, ram_1_data};  // AND_Gate and_1, 32 bits wide
endmodule
