// Logisim project ControlUnit.circ as structural Verilog: 3 circuits, main circuit ControlUnit
// Control Unit
module ControlUnit (
  input  [5:0] in_1,
  input  [5:0] in_2,
  output out_3,
  output out_4,
  output out_5,
  output out_6,
  output out_7,
  output out_8,
  output out_9,
  output [3:0] out_10
);

  wire [2:0] main_decoder_1_aluop_2_0;

  Main_Decoder main_decoder_1 (
    .Op_5_0(in_1), .MemtoReg(out_4), .MemWrite(out_5), .Branch(out_6), .ALUSrc(out_7), .RegDst(out_8),
    .RegWrite(out_9), .Jump(out_3), .ALUOp_2_0(main_decoder_1_aluop_2_0));
  ALU_Decoder alu_decoder_1 (.Funct_5_0(in_2), .ALUCtrl_3_0(out_10), .ALUOp_2_0(main_decoder_1_aluop_2_0));
endmodule

module Main_Decoder (
  input  [5:0] Op_5_0,
  output MemtoReg,
  output MemWrite,
  output Branch,
  output ALUSrc,
  output RegDst,
  output RegWrite,
  output Jump,
  output [2:0] ALUOp_2_0
);

  wire and_4_out, and_5_out, and_8_out, and_9_out;

  and and_1 (MemWrite, Op_5_0[3], Op_5_0[1]);
  or or_1 (ALUSrc, Op_5_0[1], Op_5_0[3]);
  and and_2 (Branch, ~Op_5_0[3], Op_5_0[2]);  // AND_Gate
  and and_3 (RegDst, ~Op_5_0[3], ~Op_5_0[1]);  // AND_Gate
  and and_4 (and_4_out, ~Op_5_0[2], ~Op_5_0[1]);  // AND_Gate
  and and_5 (and_5_out, Op_5_0[5], ~Op_5_0[3]);  // AND_Gate
  and and_6 (Jump, Op_5_0[1], ~Op_5_0[0]);  // AND_Gate
  and and_7 (ALUOp_2_0[1], ~Op_5_0[3], ~Op_5_0[2], ~Op_5_0[1]);  // AND_Gate
  and and_8 (and_8_out, ~Op_5_0[3], Op_5_0[2]);  // AND_Gate
  and and_9 (and_9_out, Op_5_0[4], Op_5_0[1]);
  or or_2 (RegWrite, and_4_out, Op_5_0[4], and_5_out);
  or or_3 (ALUOp_2_0[0], and_8_out, and_9_out);

  assign ALUOp_2_0[2] = Op_5_0[4];
  assign MemtoReg = Op_5_0[1];
endmodule

module ALU_Decoder (
  input  [2:0] ALUOp_2_0,
  input  [5:0] Funct_5_0,
  output [3:0] ALUCtrl_3_0
);

  wire and_1_out, and_2_out, and_3_out, and_4_out, and_5_out, and_6_out;

  and and_1 (and_1_out, ALUOp_2_0[1], Funct_5_0[4]);
  and and_2 (and_2_out, ALUOp_2_0[1], Funct_5_0[1]);
  or or_1 (ALUCtrl_3_0[3], and_1_out, ALUOp_2_0[2]);
  or or_2 (ALUCtrl_3_0[2], ALUOp_2_0[0], and_2_out);
  and and_3 (and_3_out, ~ALUOp_2_0[2], ~ALUOp_2_0[1]);  // AND_Gate
  or or_3 (ALUCtrl_3_0[1], and_3_out, and_4_out);
  and and_4 (and_4_out, ~ALUOp_2_0[2], ~Funct_5_0[2]);  // AND_Gate
  and and_5 (and_5_out, ALUOp_2_0[1], Funct_5_0[0]);
  or or_4 (ALUCtrl_3_0[0], and_5_out, and_6_out);
  and and_6 (and_6_out, ALUOp_2_0[1], Funct_5_0[3], ~Funct_5_0[2]);  // AND_Gate
endmodule
