// Logisim project Hazard_Detect.circ as structural Verilog: 1 circuit, main circuit Hazard_Detect
module Hazard_Detect (
  input  in_1,
  input  [4:0] in_2,
  input  [4:0] in_3,
  input  [4:0] in_4,
  output out_5,
  output out_6,
  output out_7
);

  wire comparator_1_eq, comparator_2_eq, or_1_out;

  Comparator #(.width(5)) comparator_1 (.a(in_2), .b(in_3), .eq(comparator_1_eq));  // open: gt, lt
  Comparator #(.width(5)) comparator_2 (.a(in_3), .b(in_4), .eq(comparator_2_eq));  // open: gt, lt
  or or_1 (or_1_out, comparator_1_eq, comparator_2_eq);
  and and_1 (out_7, in_1, or_1_out);
  not not_1 (out_5, out_7);
  not not_2 (out_6, out_7);
endmodule
