// Logisim project Hazard_Forwarding.circ as structural Verilog: 2 circuits, main circuit Data_Hazard_Forwarding
module Data_Hazard_Forwarding (
  input  RegWriteM,
  input  RegWriteW,
  input  [4:0] ID_EX_RegRs,
  input  [4:0] EX_MEM_RegRd,
  input  [4:0] ID_EX_RegRt,
  input  [4:0] MEM_WB_RegRd,
  output [1:0] MUX_A,
  output [1:0] MUX_B
);

  wire comparator_1_eq, comparator_2_eq, comparator_3_eq, comparator_4_eq, not_1_out, not_2_out, or_1_out;

  or or_1 (or_1_out, RegWriteM, RegWriteW);
  Comparator #(.width(5)) comparator_1 (.a(ID_EX_RegRs), .b(EX_MEM_RegRd), .eq(comparator_1_eq));  // open: gt, lt
  Comparator #(.width(5)) comparator_2 (.a(EX_MEM_RegRd), .b(ID_EX_RegRt), .eq(comparator_2_eq));  // open: gt, lt
  Comparator #(.width(5)) comparator_3 (.a(ID_EX_RegRs), .b(MEM_WB_RegRd), .eq(comparator_3_eq));  // open: gt, lt
  Comparator #(.width(5)) comparator_4 (.a(MEM_WB_RegRd), .b(ID_EX_RegRt), .eq(comparator_4_eq));  // open: gt, lt
  not not_1 (not_1_out, comparator_1_eq);
  not not_2 (not_2_out, comparator_2_eq);
  and and_1 (MUX_A[1], or_1_out, not_1_out, comparator_3_eq);
  and and_2 (MUX_A[0], or_1_out, comparator_1_eq);
  and and_3 (MUX_B[1], or_1_out, not_2_out, comparator_4_eq);
  and and_4 (MUX_B[0], or_1_out, comparator_2_eq);

  // Notes on the sheet:
  //   RegWriteW: pull=up
  //   No Hazard X -> MUX : 00
  //   EX_Hazard -> MUX : 01
  //   MEM_Hazard -> MUX : 10
  //   ALU_A
  //   ALU_B
  //   ALU_A
  //   ALU_B
endmodule

module Ctrl_Hazard_Forwarding (
  input  [4:0] RsD,
  input  [4:0] RdM,
  input  RegWriteM,
  input  [4:0] RtD,
  output ForwardAD,
  output ForwardBD
);

  wire comparator_1_eq, comparator_2_eq, comparator_3_eq, comparator_4_eq;

  Comparator #(.width(5)) comparator_1 (.a(RsD), .b({5{1'b0}}), .eq(comparator_1_eq));  // open: gt, lt
  Comparator #(.width(5)) comparator_2 (.a(RsD), .b(RdM), .eq(comparator_2_eq));  // open: gt, lt
  Comparator #(.width(5)) comparator_3 (.a(RdM), .b(RtD), .eq(comparator_3_eq));  // open: gt, lt
  Comparator #(.width(5)) comparator_4 (.a({5{1'b0}}), .b(RtD), .eq(comparator_4_eq));  // open: gt, lt
  and and_1 (ForwardAD, ~comparator_1_eq, comparator_2_eq, RegWriteM);  // AND_Gate
  and and_2 (ForwardBD, RegWriteM, comparator_3_eq, ~comparator_4_eq);  // AND_Gate
endmodule
